// Logisim project Processador.circ as structural Verilog: 3 circuits, main circuit main
module main (
);

  wire button_1_out, Clk, comparator_1_eq, comparator_1_lt, M_B_ULA, M_rd, multiplexer_1_out, not_1_out,
       not_2_out, or_1_out, W_breg, W_mem;
  wire [1:0] M_D_breg, M_sel_branch, M_sel_pc;
  wire [3:0] Banco_Instrucoes_data, Banco_Instrucoes_data_2, Funct_imm, multiplexer_5_out, multiplexer_7_out;
  wire [7:0] multiplexer_6_out;
  wire [11:0] Banco_Instrucoes_data_3;
  wire [19:0] A, B, bancoderegistradores_1_rd_out, data, Imm8, Imm12, multiplexer_2_out, multiplexer_3_out,
       multiplexer_4_out, multiplexer_8_out, PC_1, PC_B, PC_J, PC_q, ram_1_dout, ula_1_c;

  Clock clock_1 (.out(Clk));
  Multiplexer #(.select(2)) multiplexer_1 (
    .in0(comparator_1_eq), .in1(not_1_out), .in2(comparator_1_lt), .in3(not_2_out), .out(multiplexer_1_out),
    .sel(M_sel_branch));
  not not_1 (not_1_out, comparator_1_eq);
  Comparator #(.width(20)) comparator_1 (.a(A), .b(B), .eq(comparator_1_eq), .lt(comparator_1_lt));  // open: gt
  Multiplexer #(.width(20)) multiplexer_2 (.in0(PC_1), .in1(PC_B), .out(multiplexer_2_out), .sel(multiplexer_1_out));
  not not_2 (not_2_out, comparator_1_lt);
  Multiplexer #(.select(2), .width(20)) multiplexer_3 (
    .in0(PC_1), .in1(multiplexer_2_out), .in2(PC_J), .in3(data), .out(multiplexer_3_out), .sel(M_sel_pc));
  Button button_1 (.out(button_1_out));
  Multiplexer #(.width(20)) multiplexer_4 (
    .in0(multiplexer_3_out), .in1({20{1'b0}}), .out(multiplexer_4_out), .sel(button_1_out));
  Register #(.width(20)) PC (.D(multiplexer_4_out), .en(1'b1), .clk(Clk), .Q(PC_q));  // open: clr
  Adder #(.width(20)) adder_1 (.a(PC_q), .b(20'h1), .out(PC_1));  // open: cin, cout
  Adder #(.width(20)) adder_2 (.a(PC_q), .b(Imm12), .out(PC_J));  // open: cin, cout
  Adder #(.width(20)) adder_3 (.a(PC_q), .b(Imm8), .out(PC_B));  // open: cin, cout
  ROM #(.addrWidth(20), .dataWidth(20)) Banco_Instrucoes (
    .addr(PC_q), .data({Banco_Instrucoes_data_3, Banco_Instrucoes_data_2, Banco_Instrucoes_data}));
  ROM #(.addrWidth(4), .dataWidth(14)) Unidade_Controle (
    .addr(Banco_Instrucoes_data),
    .data({Funct_imm, M_sel_branch, M_sel_pc, M_D_breg, W_mem, M_B_ULA, W_breg, M_rd}));
  Multiplexer #(.width(4)) multiplexer_5 (
    .in0(4'b0000), .in1(Banco_Instrucoes_data_2), .out(multiplexer_5_out), .sel(M_rd));
  assign Imm12 = {{8{Banco_Instrucoes_data_3[11]}}, Banco_Instrucoes_data_3};  // Bit_Extender bit_extender_1
  assign Imm8 = {{12{multiplexer_6_out[7]}}, multiplexer_6_out};  // Bit_Extender bit_extender_2
  Multiplexer #(.width(8)) multiplexer_6 (
    .in0({Banco_Instrucoes_data_3[11:8], Banco_Instrucoes_data_2}), .in1(Banco_Instrucoes_data_3[11:4]),
    .out(multiplexer_6_out), .sel(M_rd));
  or or_1 (or_1_out, Banco_Instrucoes_data[0], Banco_Instrucoes_data[1], Banco_Instrucoes_data[2], Banco_Instrucoes_data[3]);
  BancoDeRegistradores bancoderegistradores_1 (
    .DADO(data), .rd(multiplexer_5_out), .rs1(Banco_Instrucoes_data_3[3:0]),
    .rs2(Banco_Instrucoes_data_3[7:4]), .clk(Clk), .W(W_breg), .rd_out(bancoderegistradores_1_rd_out), .A(A),
    .B(B));
  Multiplexer #(.width(4)) multiplexer_7 (
    .in0(Banco_Instrucoes_data_3[11:8]), .in1(Funct_imm), .out(multiplexer_7_out), .sel(or_1_out));
  Multiplexer #(.width(20)) multiplexer_8 (.in0(B), .in1(Imm8), .out(multiplexer_8_out), .sel(M_B_ULA));
  Multiplexer #(.select(2), .width(20)) multiplexer_9 (
    .in0(ula_1_c), .in1(ram_1_dout), .in2(PC_1), .out(data), .sel(M_D_breg));  // open: in3
  ULA ula_1 (.rd(bancoderegistradores_1_rd_out), .A(A), .B(multiplexer_8_out), .OPULA(multiplexer_7_out), .C(ula_1_c));
  RAM #(.addrWidth(20), .dataWidth(20)) ram_1 (
    .addr(ula_1_c), .we(W_mem), .oe(1'b1), .clk(Clk), .din(bancoderegistradores_1_rd_out), .dout(ram_1_dout));

  // Notes on the sheet:
  //   Reset
  //   contents of Banco_Instrucoes (hex, n*v repeats v):
  //   f011 7021 124 235
  //   contents of Unidade_Controle (hex, n*v repeats v):
  //   3 7 2407 2807 d 17 40 140 240 340 a3 c7
  //   opcode
  //   UC
  //   funct tipo R
endmodule

module BancoDeRegistradores (
  input  [19:0] DADO,
  input  [3:0] rd,
  input  [3:0] rs1,
  input  [3:0] rs2,
  input  clk,
  input  W,
  output [19:0] rd_out,
  output [19:0] A,
  output [19:0] B
);

  wire w00, w01, w02, w03, w04, w05, w06, w07, w08, w09, w10, w11, w12, w13, w14, w15;
  wire [19:0] vr00, vr01, vr02, vr03, vr04, vr05, vr06, vr07, vr08, vr09, vr10, vr11, vr12, vr13;

  Register #(.width(20)) R01 (.D(DADO), .en(w01), .clk(clk), .Q(vr01));  // open: clr
  Register #(.width(20)) R02 (.D(DADO), .en(w02), .clk(clk), .Q(vr02));  // open: clr
  Register #(.width(20)) R03 (.D(DADO), .en(w03), .clk(clk), .Q(vr03));  // open: clr
  Register #(.width(20)) R04 (.D(DADO), .en(w04), .clk(clk), .Q(vr04));  // open: clr
  Register #(.width(20)) R05 (.D(DADO), .en(w05), .clk(clk), .Q(vr05));  // open: clr
  Register #(.width(20)) R06 (.D(DADO), .en(w06), .clk(clk), .Q(vr06));  // open: clr
  Register #(.width(20)) R07 (.D(DADO), .en(w07), .clk(clk), .Q(vr07));  // open: clr
  Register #(.width(20)) R08 (.D(DADO), .en(w08), .clk(clk), .Q(vr08));  // open: clr
  Register #(.width(20)) R09 (.D(DADO), .en(w09), .clk(clk), .Q(vr09));  // open: clr
  Register #(.width(20)) R10 (.D(DADO), .en(w10), .clk(clk), .Q(vr10));  // open: clr
  Register #(.width(20)) R11 (.D(DADO), .en(w11), .clk(clk), .Q(vr11));  // open: clr
  Register #(.width(20)) R12 (.D(DADO), .en(w12), .clk(clk), .Q(vr12));  // open: clr
  Register #(.width(20)) R13 (.D(DADO), .en(w13), .clk(clk), .Q(vr13));  // open: clr
  Register #(.width(20)) R14 (.D(DADO), .en(w14), .clk(clk), .Q(vr00));  // open: clr
  Register #(.width(20)) R15 (.D(DADO), .en(w15), .clk(clk), .Q(vr00));  // open: clr
  Demultiplexer #(.select(4)) demultiplexer_1 (
    .out0(w00), .out1(w01), .out2(w02), .out3(w03), .out4(w04), .out5(w05), .out6(w06), .out7(w07),
    .out8(w08), .out9(w09), .out10(w10), .out11(w11), .out12(w12), .out13(w13), .out14(w14), .out15(w15),
    .in(W), .sel(rd));
  Multiplexer #(.select(4), .width(20)) multiplexer_1 (
    .in0(vr00), .in1(vr01), .in2(vr02), .in3(vr03), .in4(vr04), .in5(vr05), .in6(vr06), .in7(vr07),
    .in8(vr08), .in9(vr09), .in10(vr10), .in11(vr11), .in12(vr12), .in13(vr13), .in14(vr00), .in15(vr00),
    .out(rd_out), .sel(rd));
  Multiplexer #(.select(4), .width(20)) multiplexer_2 (
    .in0(vr00), .in1(vr01), .in2(vr02), .in3(vr03), .in4(vr04), .in5(vr05), .in6(vr06), .in7(vr07),
    .in8(vr08), .in9(vr09), .in10(vr10), .in11(vr11), .in12(vr12), .in13(vr13), .in14(vr00), .in15(vr00),
    .out(A), .sel(rs1));
  Multiplexer #(.select(4), .width(20)) multiplexer_3 (
    .in0(vr00), .in1(vr01), .in2(vr02), .in3(vr03), .in4(vr04), .in5(vr05), .in6(vr06), .in7(vr07),
    .in8(vr08), .in9(vr09), .in10(vr10), .in11(vr11), .in12(vr12), .in13(vr13), .in14(vr00), .in15(vr00),
    .out(B), .sel(rs2));
  // also tied to GND on the sheet: {vr00[0], vr00[1], vr00[2], vr00[3], vr00[4], vr00[5], vr00[6], vr00[7], vr00[8], vr00[9], vr00[10], vr00[11], vr00[12], vr00[13], vr00[14], vr00[15], vr00[16], vr00[17], vr00[18], vr00[19]}

  // Other names for the same wires on the sheet: vr14[19:0] = vr00; vr15[19:0] = vr00; WD[19:0] = DADO
endmodule

module ULA (
  input  [19:0] rd,
  input  [19:0] A,
  input  [19:0] B,
  input  [3:0] OPULA,
  output [19:0] C
);

  wire [19:0] multiplier_1_out, OP0000, OP0001, OP0010, OP0011, OP0100, OP0101, OP0110, OP0111, OP1000,
       OP1001, OP1010, OP1011, OP1100;

  Multiplier #(.width(20)) multiplier_1 (.a(A), .b(B), .out(multiplier_1_out));  // open: cin, cout
  Adder #(.width(20)) adder_1 (.a(A), .b(B), .out(OP0000));  // open: cin, cout
  Subtractor #(.width(20)) subtractor_1 (.a(A), .b(B), .out(OP0001));  // open: bin, bout
  Multiplier #(.width(20)) multiplier_2 (.a(A), .b(B), .out(OP0010));  // open: cin, cout
  Divider #(.width(20)) divider_1 (.a(A), .b(B), .out(OP0011), .rem(OP0100));  // open: upper
  assign OP0101 = A | B;  // OR_Gate or_1, 20 bits wide
  assign OP0110 = A & B;  // AND_Gate and_1, 20 bits wide
  assign OP0111 = A ^ B;  // XOR_Gate xor_1, 20 bits wide
  assign OP1000 = ~A;  // NOT_Gate not_1, 20 bits wide
  Shifter #(.width(20)) shifter_1 (.in(A), .\dist (B[4:0]), .out(OP1001));
  Shifter #(.shift("lr"), .width(20)) shifter_2 (.in(A), .\dist (B[4:0]), .out(OP1010));
  Shifter #(.shift("ar"), .width(20)) shifter_3 (.in(A), .\dist (B[4:0]), .out(OP1011));
  Adder #(.width(20)) adder_2 (.a(multiplier_1_out), .b(rd), .out(OP1100));  // open: cin, cout
  Multiplexer #(.select(4), .width(20)) multiplexer_1 (
    .in0(OP0000), .in1(OP0001), .in2(OP0010), .in3(OP0011), .in4(OP0100), .in5(OP0101), .in6(OP0110),
    .in7(OP0111), .in8(OP1000), .in9(OP1001), .in10(OP1010), .in11(OP1011), .in12(OP1100), .out(C),
    .sel(OPULA));  // open: in13, in14, in15

  // Notes on the sheet:
  //   ADD
  //   SUB
  //   MUL
  //   DIV
  //   OR
  //   AND
  //   XOR
  //   NOT
  //   SLL
  //   SRL
  //   SRA
  //   MAC
  //   REM
endmodule
